# Fritzing sketch LXF207-SpaceGame (saved by Fritzing 0.9.1b)
breadboards: 1

parts:
  S3 = Momentary Switch [package=ksa_sealed_tac_switch]
  S4 = Momentary Switch [package=ksa_sealed_tac_switch]
  S5 = Momentary Switch [package=ksa_sealed_tac_switch]
  LED1 = smd LED [color="Yellow (595nm)" package="0805 [SMD]"]
  LED2 = smd LED [color="Red (633nm)" package="0805 [SMD]"]
  LED3 = smd LED [color="Green (555nm)" package="0805 [SMD]"]
  R1 = Resistor [tolerance=±5% resistance=220 package="0805 [SMD]"]
  R2 = Resistor [tolerance=±5% resistance=220 package="0805 [SMD]"]
  R3 = Resistor [tolerance=±5% resistance=220 package="0805 [SMD]"]
  Raspberry_Pi1 = Raspberry Pi B+

nets:
  N1: S3.2, S3.4, S4.2, S5.2, R1.Pin_0, R2.Pin_0, R3.Pin_0, Raspberry_Pi1.GPIO24, Raspberry_Pi1.GPIO23, Raspberry_Pi1.GND
  N2: S4.4, Raspberry_Pi1.GPIO2
  N3: S5.4, Raspberry_Pi1.GPIO15, Raspberry_Pi1.GPIO14
  N4: LED1.cathode, R2.Pin_1
  N5: LED1.anode, Raspberry_Pi1.GPIO27
  N6: LED2.cathode, R1.Pin_1
  N7: LED2.anode, Raspberry_Pi1.GPIO17
  N8: LED3.cathode, R3.Pin_1
  N9: LED3.anode, Raspberry_Pi1.GPIO22
